# Fritzing sketch Schema_Arduino (saved by Fritzing 0.9.2b)
breadboards: 1

parts:
  Composant1 = Arduino Nano (Rev3.0)
  R1 = Temperature Sensor (Thermistor) [thermistor_type=NTC package=THT]
  U1 = ESP8266 WiFi Module [part_number=ESP8266]
  R2 = Resistor [tolerance=±5% resistance=220 package="2010 [SMD]"]
  PIR2 = PIR sensor

nets:
  N1: Composant1.D0/RX, U1.TXD
  GND: Composant1.GND, R1.pin_1, PIR2.GND
  N2: Composant1.D7, PIR2.SIG
  5V: Composant1.5V, PIR2.VDD
  N3: Composant1.A4, R1.pin_0, R2.Pin_0
  3V3: Composant1.3V3, U1.VCC, U1.CH_PD

custom parts:
  ESP8266 WiFi Module: Generic WiFi Module based on the ESP8266 with onboard PCB antenna and UART communications
